# Fritzing sketch FirstWaveISACBeacon_PCBv2.6 (saved by Fritzing 0.9.3b)
circuit board: 7.08194cm x 3.22982cm
breadboards: 1

parts:
  Adafruit_Trinket_Pro_5V = Adafruit Pro Trinket 5V 16MHz [part_number="Adafruit #2000"]
  DFPlayer = DFRobot DFPlayer Mini [part_number=DFR0299]
  Plus_Button = Momentary Switch [package=ksa_sealed_tac_switch]
  Minus_Button = Momentary Switch [package=ksa_sealed_tac_switch]
  Neopixel_16 = 16 NeoPixel Ring [part_number=1463]
  Speaker = SPEAKER [package=pcb_mount_speaker]
  100k = Resistor [tolerance=±5% resistance=100k package=THT]
  1K = Resistor [tolerance=±5% resistance=1k package=THT]
  100k_2 = Resistor [tolerance=±5% resistance=100k package=THT]
  NeoPixel_16_[IGV] = rounded female pin header, 3 pins [form="♀ (female rounded)"]
  Speaker_2 = rounded female pin header, 2 pins [form="♀ (female rounded)"]
  [+G-]_Buttons = rounded female pin header, 3 pins [form="♀ (female rounded)"]
  6_3v_330uF = Capacitor Polarized [package=cpol-radial-100uf-25v]
  6_3v_330uF1 = Capacitor Polarized [package=cpol-radial-100uf-25v]

nets:
  GND: Adafruit_Trinket_Pro_5V.GND, DFPlayer.GND-1, DFPlayer.GND-2, Plus_Button.1, Minus_Button.3, Neopixel_16.GND, 100k.Pin_1, NeoPixel_16_[IGV].pin2, [+G-]_Buttons.pin2, 6_3v_330uF.-, 6_3v_330uF1.-
  +5V: Adafruit_Trinket_Pro_5V.+5V, DFPlayer.VCC, Neopixel_16.VDD, 100k_2.Pin_1, NeoPixel_16_[IGV].pin3, 6_3v_330uF.+, 6_3v_330uF1.+
  N1: Adafruit_Trinket_Pro_5V.D6, Neopixel_16.IN, NeoPixel_16_[IGV].pin1
  N2: Adafruit_Trinket_Pro_5V.D5, 1K.Pin_1
  N3: Adafruit_Trinket_Pro_5V.D3, DFPlayer.TX
  N4: Adafruit_Trinket_Pro_5V.A0, Minus_Button.1, [+G-]_Buttons.pin1
  N5: Adafruit_Trinket_Pro_5V.A1, Plus_Button.3, [+G-]_Buttons.pin3
  N6: Adafruit_Trinket_Pro_5V.A4, DFPlayer.SPK_2, Speaker.-, 100k.Pin_0, 100k_2.Pin_0, Speaker_2.pin2
  N7: DFPlayer.RX, 1K.Pin_0
  N8: DFPlayer.SPK_1, Speaker.+, Speaker_2.pin1

notes:
  SHD ISAC Beacon
  v2.6 by Cameron G.
  First Wave

custom parts:
  Adafruit Pro Trinket 5V 16MHz: Trinket's got a big sister in town - the Pro Trinket 5V! Pro Trinket combines everything you love about Trinket with the familiarity of the common core Arduino chip, the ATmega328. It's like an Arduino Pro Mini with more pins and USB tossed in, so delicious. Trinket's a year old now, and while its been great to see tons of tiny projects, sometimes you just need more pins, more FLASH, and more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
  16 NeoPixel Ring: 16 ultra bright smart LED NeoPixels are arranged in a circle with 1.75" (44.5mm) outer diameter. The rings are 'chainable' - connect the output pin of one to the input pin of another. Use only one microcontroller pin to control as many as you can chain together! Each LED is addressable as the driver chip is inside the LED. Each one has ~18mA constant current drive so the color will be very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
